// Logisim project Bilgisayar_Devresi.circ as structural Verilog: 19 circuits, main circuit main
module main (
  input  [3:0] \ınpr ,
  input  in_2,
  output [7:0] out_3,
  output cout,
  output [3:0] out_5
);

  wire and_1_out, clock_1_out, main_cont_1_dr_load, main_cont_1_hlt, main_cont_1_outtr__load;
  wire [1:0] main_cont_1_m_ar__bus_load, \main_cont_1_ır_bus_load ;
  wire [2:0] main_cont_1_ar__bus_inc_load, main_cont_1_pc__inc_bus_load;
  wire [3:0] ac_output, ar_output, dr_output, main_cont_1_ac_bus_clr_inc_load, n4bit_alu_1_out_13,
       outTr_output, pc_output, \ır__4_7 ;
  wire [6:0] main_cont_1_out_11;
  wire [7:0] ram_1_data;

  Clock clock_1 (.out(clock_1_out));
  main_cont main_cont_1 (
    .\ır__4_7 (\ır__4_7 ), .clk(and_1_out), .hlt(main_cont_1_hlt),
    .ar__bus_inc_load(main_cont_1_ar__bus_inc_load), .pc__inc_bus_load(main_cont_1_pc__inc_bus_load),
    .dr_load(main_cont_1_dr_load), .outTr__load(main_cont_1_outtr__load),
    .ac_bus_clr_inc_load(main_cont_1_ac_bus_clr_inc_load), .\ır_bus_load (\main_cont_1_ır_bus_load ),
    .m_ar__bus_load(main_cont_1_m_ar__bus_load), .out_11(main_cont_1_out_11));
  and and_1 (and_1_out, ~main_cont_1_hlt, clock_1_out);  // AND_Gate
  _4bit_alu u_4bit_alu_1 (
    .ac(ac_output), .dr(dr_output), .\ınpr (\ınpr ), .\and (main_cont_1_out_11[0]),
    .add(main_cont_1_out_11[1]), .cma(main_cont_1_out_11[2]), .ld_dr(main_cont_1_out_11[3]),
    .\ld_ınpr (main_cont_1_out_11[4]), .\cır (main_cont_1_out_11[5]), .\cıl (main_cont_1_out_11[6]),
    .clk(and_1_out), .clear(in_2), .out_13(n4bit_alu_1_out_13), .cout(cout));
  RAM #(.addrWidth(4), .bus("separate")) ram_1 (
    .addr(ar_output), .din(out_3), .data(ram_1_data), .str(main_cont_1_m_ar__bus_load[0]), .clk(and_1_out));  // open: sel, ld, clr
  _4_REG ar (
    .INPUT(out_3[3:0]), .CLK(and_1_out), .LD(main_cont_1_ar__bus_inc_load[0]),
    .INC(main_cont_1_ar__bus_inc_load[1]), .OUTPUT(ar_output));  // open: CLR
  _4_REG pc (
    .INPUT(out_3[3:0]), .CLK(and_1_out), .LD(main_cont_1_pc__inc_bus_load[0]),
    .INC(main_cont_1_pc__inc_bus_load[2]), .OUTPUT(pc_output));  // open: CLR
  _4_REG dr (.INPUT(out_3[3:0]), .CLK(and_1_out), .LD(main_cont_1_dr_load), .OUTPUT(dr_output));  // open: INC, CLR
  _4_REG ac (
    .INPUT(n4bit_alu_1_out_13), .CLK(and_1_out), .LD(main_cont_1_ac_bus_clr_inc_load[0]),
    .INC(main_cont_1_ac_bus_clr_inc_load[1]), .CLR(main_cont_1_ac_bus_clr_inc_load[2]), .OUTPUT(ac_output));
  _4_REG outTr (
    .INPUT(out_3[3:0]), .CLK(and_1_out), .LD(main_cont_1_outtr__load), .OUTPUT(outTr_output));  // open: INC, CLR
  Ir \u_ır  (.in_1(out_3), .clk(and_1_out), .load(\main_cont_1_ır_bus_load [0]), ._0_3(out_5), ._4_7(\ır__4_7 ));
  // Probe on ar_output
  // Probe on pc_output
  // Probe on dr_output
  // Probe on outTr_output
  // Probe on \ır__4_7 
  assign out_3 = main_cont_1_m_ar__bus_load[1] ? ram_1_data : 8'bz;  // Controlled_Buffer controlled_buffer_1
  // Probe on ac_output
  assign out_3 = \main_cont_1_ır_bus_load [1] ? {4'b0000, out_5} : 8'bz;  // Controlled_Buffer controlled_buffer_2
  assign out_3 = main_cont_1_ar__bus_inc_load[2] ? {4'b0000, ar_output} : 8'bz;  // Controlled_Buffer controlled_buffer_3
  assign out_3 = main_cont_1_pc__inc_bus_load[1] ? {4'b0000, pc_output} : 8'bz;  // Controlled_Buffer controlled_buffer_4
  assign out_3 = main_cont_1_ac_bus_clr_inc_load[3] ? {4'b0000, ac_output} : 8'bz;  // Controlled_Buffer controlled_buffer_5
endmodule

// reg.
module _4_REG (
  input  INC,
  input  LD,
  input  [3:0] INPUT,
  input  CLK,
  input  CLR,
  output [3:0] OUTPUT
);

  wire and_1_out, and_2_out, and_3_out, and_4_out, and_5_out, and_6_out, and_7_out, and_8_out, and_9_out,
       and_10_out, and_11_out, and_12_out, not_1_out, not_2_out, not_3_out, not_4_out, not_5_out, not_6_out,
       or_1_out, or_2_out, or_3_out, or_4_out, or_5_out, or_6_out, or_7_out, or_8_out;

  not not_1 (not_1_out, LD);
  not not_2 (not_2_out, not_1_out);
  not not_3 (not_3_out, INPUT[0]);
  not not_4 (not_4_out, INPUT[1]);
  not not_5 (not_5_out, INPUT[2]);
  not not_6 (not_6_out, INPUT[3]);
  and and_1 (and_1_out, INC, not_1_out);
  and and_2 (and_2_out, not_2_out, INPUT[0]);
  and and_3 (and_3_out, not_2_out, not_3_out);
  and and_4 (and_4_out, not_2_out, INPUT[1]);
  and and_5 (and_5_out, not_2_out, not_4_out);
  and and_6 (and_6_out, not_2_out, INPUT[2]);
  and and_7 (and_7_out, not_2_out, not_5_out);
  and and_8 (and_8_out, not_2_out, INPUT[3]);
  and and_9 (and_9_out, not_2_out, not_6_out);
  and and_10 (and_10_out, and_1_out, OUTPUT[0]);
  and and_11 (and_11_out, and_1_out, OUTPUT[0], OUTPUT[1]);
  and and_12 (and_12_out, and_1_out, OUTPUT[0], OUTPUT[1], OUTPUT[2]);
  or or_1 (or_1_out, and_2_out, and_1_out);
  or or_2 (or_2_out, and_3_out, and_1_out);
  or or_3 (or_3_out, and_4_out, and_10_out);
  or or_4 (or_4_out, and_10_out, and_5_out);
  or or_5 (or_5_out, and_6_out, and_11_out);
  or or_6 (or_6_out, and_11_out, and_7_out);
  or or_7 (or_7_out, and_8_out, and_12_out);
  or or_8 (or_8_out, and_12_out, and_9_out);
  J_K_Flip_Flop j_k_ff_1 (.J(or_1_out), .clk(CLK), .K(or_2_out), .Q(OUTPUT[0]), .reset(CLR));  // open: Qn, preset, en
  J_K_Flip_Flop j_k_ff_2 (.J(or_3_out), .clk(CLK), .K(or_4_out), .Q(OUTPUT[1]), .reset(CLR));  // open: Qn, preset, en
  J_K_Flip_Flop j_k_ff_3 (.J(or_5_out), .clk(CLK), .K(or_6_out), .Q(OUTPUT[2]), .reset(CLR));  // open: Qn, preset, en
  J_K_Flip_Flop j_k_ff_4 (.J(or_7_out), .clk(CLK), .K(or_8_out), .Q(OUTPUT[3]), .reset(CLR));  // open: Qn, preset, en
endmodule

module pc (
  input  t0,
  input  t1,
  input  t3,
  input  t4,
  input  d4,
  input  d5,
  input  d6,
  output LD,
  output INC,
  output BUS
);

  wire and_1_out, and_2_out, and_3_out, or_1_out;

  or or_1 (or_1_out, d4, d6);
  and and_1 (and_1_out, t3, d5);
  and and_2 (and_2_out, t3, or_1_out);
  and and_3 (and_3_out, t4, d5);
  or or_2 (BUS, t0, and_1_out);
  or or_3 (LD, and_2_out, and_3_out);

  assign INC = t1;
endmodule

module Ir (
  input  [7:0] in_1,
  input  clk,
  input  load,
  output [3:0] _0_3,
  output [3:0] _4_7
);

  _4_REG u_4_reg_1 (.INPUT(in_1[7:4]), .CLK(clk), .LD(load), .INC(1'b0), .CLR(1'b0), .OUTPUT(_4_7));
  _4_REG u_4_reg_2 (.INPUT(in_1[3:0]), .CLK(clk), .LD(load), .INC(1'b0), .CLR(1'b0), .OUTPUT(_0_3));
endmodule

module Dr (
  input  d0,
  input  d1,
  input  d2,
  input  t3,
  output load
);

  wire or_1_out;

  or or_1 (or_1_out, d0, d1, d2);
  and and_1 (load, or_1_out, t3);
endmodule

module Ar (
  input  t0,
  input  t2,
  input  t3,
  input  t4,
  input  d4,
  input  d5,
  output load,
  output Inc,
  output bus
);

  wire and_2_out, and_3_out;

  or or_1 (load, t0, t2);
  and and_1 (Inc, t3, d5);
  and and_2 (and_2_out, d4, t3);
  and and_3 (and_3_out, t4, d5);
  or or_2 (bus, and_2_out, and_3_out);
endmodule

module Ac (
  input  d0,
  input  d1,
  input  d2,
  input  d3,
  input  d7,
  input  d9,
  input  d10,
  input  d11,
  input  d12,
  input  d13,
  input  d14,
  input  t3,
  input  t4,
  output load,
  output Inc,
  output clr,
  output bus
);

  wire and_2_out, or_1_out, or_2_out, or_3_out;

  or or_1 (or_1_out, d9, d11, d12, d13);
  or or_2 (or_2_out, d0, d1, d2);
  // AND_Gate and_1 has open pins: in0=or_1_out, in1=t3, out=open
  or or_3 (or_3_out, d3, d14);
  and and_2 (and_2_out, or_2_out, t4);
  and and_3 (Inc, d10, t3);
  and and_4 (clr, d7, t3);
  and and_5 (bus, or_3_out, t3);
  buf or_4 (load, and_2_out);  // OR_Gate
endmodule

module Ir_cnt (
  input  t1,
  input  t2,
  output load,
  output bus
);


  assign bus = t2;
  assign load = t1;
endmodule

module M_ar (
  input  d0,
  input  d1,
  input  d2,
  input  d3,
  input  d5,
  input  d6,
  input  t1,
  input  t3,
  output M_bus,
  output M_load
);

  wire and_1_out, or_1_out, or_2_out;

  or or_1 (or_1_out, d0, d1, d2, d6);
  or or_2 (or_2_out, d3, d5);
  and and_1 (and_1_out, or_1_out, t3);
  and and_2 (M_load, or_2_out, t3);
  or or_3 (M_bus, t1, and_1_out);
endmodule

module Inpr (
  input  d13,
  input  t3,
  output out_3
);

  and and_1 (out_3, d13, t3);
endmodule

module outTr (
  input  d14,
  input  t3,
  output load
);

  and and_1 (load, d14, t3);
endmodule

module counter (
  input  clk,
  input  sc_clr,
  output [3:0] out_3
);

  wire and_1_out, register_1_q;

  Counter #(.width(4), .max('hf)) counter_1 (
    .count(1'b1), .Q(out_3), .clk(clk), .clr(register_1_q));  // open: load, D, carry
  Register #(.width(1)) register_1 (.D(sc_clr), .Q(register_1_q), .clk(clk), .clr(and_1_out));  // open: en
  and and_1 (and_1_out, clk, sc_clr);
endmodule

module alu (
  input  d0,
  input  d1,
  input  d2,
  input  d9,
  input  d11,
  input  d12,
  input  d13,
  input  t3,
  input  t4,
  output \and ,
  output add,
  output \ıd_dr ,
  output cmp,
  output shr,
  output shl,
  output \ıd_ınpr 
);

  and and_1 (\and , d0, t4);
  and and_2 (add, d1, t4);
  and and_3 (\ıd_dr , d2, t4);
  and and_4 (cmp, d9, t3);
  and and_5 (shr, d11, t3);
  and and_6 (shl, d12, t3);
  and and_7 (\ıd_ınpr , d13, t3);
endmodule

module carry_elde (
  input  ac3_cout,
  input  ac3,
  input  ac0,
  input  \cır ,
  input  \cıl ,
  input  add,
  input  clk,
  input  clear,
  output out_e,
  output \ac_İ_1 ,
  output \ac_İ_1_2 ,
  output cin
);

  wire and_1_out, and_2_out, and_3_out, and_4_out, and_5_out, d_ff_1_q, not_1_out, or_1_out, or_2_out;

  or or_1 (or_1_out, ac3_cout, ac3, ac0);
  and and_1 (and_1_out, ac0, \cır );
  and and_2 (and_2_out, ac3, \cıl );
  and and_3 (and_3_out, ac3_cout, add);
  or or_2 (or_2_out, and_1_out, and_2_out, and_3_out);
  not not_1 (not_1_out, or_2_out);
  and and_4 (and_4_out, or_1_out, or_2_out);
  and and_5 (and_5_out, or_1_out, not_1_out);
  J_K_Flip_Flop j_k_ff_1 (.J(and_4_out), .clk(clk), .K(and_5_out), .Q(out_e), .reset(clear));  // open: Qn, preset, en
  D_Flip_Flop d_ff_1 (.clk(clk), .D(out_e), .Q(d_ff_1_q));  // open: Qn, preset, en, reset
  and and_6 (\ac_İ_1 , d_ff_1_q, \cıl );
  and and_7 (\ac_İ_1_2 , d_ff_1_q, \cır );
  and and_8 (cin, d_ff_1_q, add);
endmodule

module sc_clr (
  input  d0,
  input  d1,
  input  d2,
  input  d3,
  input  d4,
  input  d5,
  input  d6,
  input  d7,
  input  d8,
  input  d9,
  input  d10,
  input  d11,
  input  d12,
  input  d13,
  input  d14,
  input  t3,
  input  t4,
  output sc_clr
);

  wire and_1_out, and_2_out, or_1_out, or_2_out;

  or or_1 (or_1_out, d0, d1, d2, d5);
  or or_2 (or_2_out, d6, d7, d8, d9, d10, d11, d12, d13, d14, d3, d4);
  and and_1 (and_1_out, or_1_out, t4);
  and and_2 (and_2_out, or_2_out, t3);
  or or_3 (sc_clr, and_2_out, and_1_out);
endmodule

module _1bit_alu (
  input  dr,
  input  Inpr,
  input  ac,
  input  \and ,
  input  cin,
  input  add,
  input  cma,
  input  ld_dr,
  input  ld_Inpr,
  input  \cır ,
  input  ac_i_1,
  input  \cıl ,
  input  ac_i_1_2,
  output cout,
  output output__ac
);

  wire add_out, adder_1_out, and_out, comp_out, not_1_out, shl_out, shr_out, \ıd_dr_out , \ıd_ınpr_out ;

  Adder #(.width(1)) adder_1 (.a(ac), .b(dr), .out(adder_1_out), .cin(cin), .cout(cout));
  not not_1 (not_1_out, ac);
  and u_and (and_out, \and , ac, dr);
  and u_add (add_out, add, adder_1_out);
  and comp (comp_out, cma, not_1_out);
  and \u_ıd_dr  (\ıd_dr_out , ld_dr, dr);
  and \u_ıd_ınpr  (\ıd_ınpr_out , ld_Inpr, Inpr);
  and shr (shr_out, \cır , ac_i_1);
  and shl (shl_out, \cıl , ac_i_1_2);
  or or_1 (output__ac, and_out, add_out, comp_out, \ıd_dr_out , \ıd_ınpr_out , shr_out, shl_out);
endmodule

module _4bit_alu (
  input  [3:0] ac,
  input  [3:0] dr,
  input  [3:0] \ınpr ,
  input  \and ,
  input  add,
  input  cma,
  input  ld_dr,
  input  \ld_ınpr ,
  input  \cır ,
  input  \cıl ,
  input  clk,
  input  clear,
  output [3:0] out_13,
  output cout
);

  wire \carry_elde_1_ac_i̇_1 , \carry_elde_1_ac_i̇_1_2 , carry_elde_1_cin, n1bit_alu_1_cout,
       n1bit_alu_2_cout, n1bit_alu_3_cout, n1bit_alu_4_cout;
  wire [4:3] undriven;

  _1bit_alu u_1bit_alu_1 (
    .dr(dr[0]), .Inpr(\ınpr [0]), .ac(ac[0]), .\and (\and ), .cin(carry_elde_1_cin), .add(add), .cma(cma),
    .ld_dr(undriven[3]), .ld_Inpr(undriven[4]), .\cır (ld_dr), .ac_i_1(ac[1]), .\cıl (\ld_ınpr ),
    .ac_i_1_2(\carry_elde_1_ac_i̇_1 ), .cout(n1bit_alu_1_cout), .output__ac(out_13[0]));
  _1bit_alu u_1bit_alu_2 (
    .dr(dr[1]), .Inpr(\ınpr [1]), .ac(ac[1]), .\and (\and ), .cin(n1bit_alu_1_cout), .add(add), .cma(cma),
    .ld_dr(undriven[3]), .ld_Inpr(undriven[4]), .\cır (ld_dr), .ac_i_1(ac[2]), .\cıl (\ld_ınpr ),
    .ac_i_1_2(ac[0]), .cout(n1bit_alu_2_cout), .output__ac(out_13[1]));
  _1bit_alu u_1bit_alu_3 (
    .dr(dr[2]), .Inpr(\ınpr [2]), .ac(ac[2]), .\and (\and ), .cin(n1bit_alu_2_cout), .add(add), .cma(cma),
    .ld_dr(undriven[3]), .ld_Inpr(undriven[4]), .\cır (ld_dr), .ac_i_1(ac[3]), .\cıl (\ld_ınpr ),
    .ac_i_1_2(ac[1]), .cout(n1bit_alu_3_cout), .output__ac(out_13[2]));
  _1bit_alu u_1bit_alu_4 (
    .dr(dr[3]), .Inpr(\ınpr [3]), .ac(ac[3]), .\and (\and ), .cin(n1bit_alu_3_cout), .add(add), .cma(cma),
    .ld_dr(undriven[3]), .ld_Inpr(undriven[4]), .\cır (ld_dr), .ac_i_1(\carry_elde_1_ac_i̇_1_2 ),
    .\cıl (\ld_ınpr ), .ac_i_1_2(ac[2]), .cout(n1bit_alu_4_cout), .output__ac(out_13[3]));
  carry_elde carry_elde_1 (
    .ac3_cout(n1bit_alu_4_cout), .ac3(ac[3]), .ac0(ac[0]), .\cır (\cır ), .\cıl (\cıl ), .add(add),
    .clk(clk), .clear(clear), .out_e(cout), .\ac_İ_1 (\carry_elde_1_ac_i̇_1 ),
    .\ac_İ_1_2 (\carry_elde_1_ac_i̇_1_2 ), .cin(carry_elde_1_cin));
endmodule

module reg_cont (
  input  t0,
  input  t1,
  input  t2,
  input  t3,
  input  t4,
  input  d0,
  input  d1,
  input  d2,
  input  d3,
  input  d4,
  input  d5,
  input  d6,
  input  d7,
  input  d8,
  input  d9,
  input  d10,
  input  d11,
  input  d12,
  input  d13,
  input  d14,
  output [2:0] ar_bus_inc_load,
  output [2:0] pc_inc_bus_load,
  output dr_load,
  output outTr_load,
  output [3:0] ac_bus_clr_inc_load,
  output [1:0] \ır_bus_load ,
  output [1:0] m_ar__bus_load
);

  Ar ar_1 (
    .t0(t0), .t2(t2), .t3(t3), .t4(t4), .d4(d4), .d5(d5), .load(ar_bus_inc_load[0]),
    .Inc(ar_bus_inc_load[1]), .bus(ar_bus_inc_load[2]));
  pc pc_1 (
    .t0(t0), .t1(t1), .t3(t3), .t4(t4), .d4(d4), .d5(d5), .d6(d6), .LD(pc_inc_bus_load[0]),
    .INC(pc_inc_bus_load[2]), .BUS(pc_inc_bus_load[1]));
  Dr dr_1 (.d0(d0), .d1(d1), .d2(d2), .t3(t3), .load(dr_load));
  outTr outtr_1 (.d14(d14), .t3(t3), .load(outTr_load));
  Ac ac_1 (
    .d0(d0), .d1(d1), .d2(d2), .d3(d3), .d7(d7), .d9(d9), .d10(d10), .d11(d11), .d12(d12), .d13(d13),
    .d14(d14), .t3(t3), .t4(t4), .load(ac_bus_clr_inc_load[0]), .Inc(ac_bus_clr_inc_load[1]),
    .clr(ac_bus_clr_inc_load[2]), .bus(ac_bus_clr_inc_load[3]));
  Ir_cnt ir_cnt_1 (.t1(t1), .t2(t2), .load(\ır_bus_load [0]), .bus(\ır_bus_load [1]));
  M_ar m_ar_1 (
    .d0(d0), .d1(d1), .d2(d2), .d3(d3), .d5(d5), .d6(d6), .t1(t1), .t3(t3), .M_bus(m_ar__bus_load[1]),
    .M_load(m_ar__bus_load[0]));
endmodule

module main_cont (
  input  [3:0] \ır__4_7 ,
  input  clk,
  output [2:0] ar__bus_inc_load,
  output [2:0] pc__inc_bus_load,
  output dr_load,
  output outTr__load,
  output [3:0] ac_bus_clr_inc_load,
  output [1:0] \ır_bus_load ,
  output [1:0] m_ar__bus_load,
  output hlt,
  output [6:0] out_11
);

  wire sc_clr_1_sc_clr;
  wire [3:0] counter_1_out_3;
  wire [4:0] decoder_2_out0;
  wire [6:0] decoder_1_out13;
  wire [14:3] decoder_1_out3;

  Decoder #(.select(4)) decoder_1 (
    .out0(decoder_1_out13[6]), .out1(decoder_1_out13[5]), .out2(decoder_1_out13[4]),
    .out3(decoder_1_out3[3]), .out4(decoder_1_out3[4]), .out5(decoder_1_out3[5]), .out6(decoder_1_out3[6]),
    .out7(decoder_1_out3[7]), .out8(decoder_1_out3[8]), .out9(decoder_1_out13[3]),
    .out10(decoder_1_out3[10]), .out11(decoder_1_out13[2]), .out12(decoder_1_out13[1]),
    .out13(decoder_1_out13[0]), .out14(decoder_1_out3[14]), .out15(hlt), .sel(\ır__4_7 ));  // open: en
  sc_clr sc_clr_1 (
    .d0(decoder_1_out3[14]), .d1(decoder_1_out13[0]), .d2(decoder_1_out13[1]), .d3(decoder_1_out13[2]),
    .d4(decoder_1_out3[10]), .d5(decoder_1_out13[3]), .d6(decoder_1_out3[8]), .d7(decoder_1_out3[7]),
    .d8(decoder_1_out3[6]), .d9(decoder_1_out3[5]), .d10(decoder_1_out3[4]), .d11(decoder_1_out3[3]),
    .d12(decoder_1_out13[4]), .d13(decoder_1_out13[5]), .d14(decoder_1_out13[6]), .t3(decoder_2_out0[3]),
    .t4(decoder_2_out0[4]), .sc_clr(sc_clr_1_sc_clr));
  Decoder #(.select(4)) decoder_2 (
    .out0(decoder_2_out0[0]), .out1(decoder_2_out0[1]), .out2(decoder_2_out0[2]), .out3(decoder_2_out0[3]),
    .out4(decoder_2_out0[4]), .sel(counter_1_out_3));  // open: out5, out6, out7, out8, out9, out10, out11, out12, out13, out14, out15, en
  counter counter_1 (.clk(clk), .sc_clr(sc_clr_1_sc_clr), .out_3(counter_1_out_3));
  reg_cont reg_cont_1 (
    .t0(decoder_2_out0[0]), .t1(decoder_2_out0[1]), .t2(decoder_2_out0[2]), .t3(decoder_2_out0[3]),
    .t4(decoder_2_out0[4]), .d0(decoder_1_out3[14]), .d1(decoder_1_out13[0]), .d2(decoder_1_out13[1]),
    .d3(decoder_1_out13[2]), .d4(decoder_1_out3[10]), .d5(decoder_1_out13[3]), .d6(decoder_1_out3[8]),
    .d7(decoder_1_out3[7]), .d8(decoder_1_out3[6]), .d9(decoder_1_out3[5]), .d10(decoder_1_out3[4]),
    .d11(decoder_1_out3[3]), .d12(decoder_1_out13[4]), .d13(decoder_1_out13[5]), .d14(decoder_1_out13[6]),
    .ar_bus_inc_load(ar__bus_inc_load), .pc_inc_bus_load(pc__inc_bus_load), .dr_load(dr_load),
    .outTr_load(outTr__load), .ac_bus_clr_inc_load(ac_bus_clr_inc_load), .\ır_bus_load (\ır_bus_load ),
    .m_ar__bus_load(m_ar__bus_load));
  alu alu_1 (
    .d0(decoder_1_out13[0]), .d1(decoder_1_out13[1]), .d2(decoder_1_out13[2]), .d9(decoder_1_out13[3]),
    .d11(decoder_1_out13[4]), .d12(decoder_1_out13[5]), .d13(decoder_1_out13[6]), .t3(decoder_2_out0[3]),
    .t4(decoder_2_out0[4]), .\and (out_11[0]), .add(out_11[1]), .\ıd_dr (out_11[2]), .cmp(out_11[3]),
    .shr(out_11[4]), .shl(out_11[5]), .\ıd_ınpr (out_11[6]));
endmodule
